# Fritzing sketch pj1 (1) (saved by Fritzing 1.0.5)
breadboards: 1

parts:
  Part1 = Arduino Uno (Rev3)
  L298N1 = L298N DC motor driver
  Mod1 = KY-022 Infrared Receiver Module [package="Breakout board"]
  U1 = LM2596 step down module  # not connected
  M2 = DC Motor [voltage_(max)=6V voltage_(min)=3V]  # not connected
  U2 = LIPO-110mAh [package=lipo-110]  # not connected

nets:
  N1: Part1.D4, L298N1.IN2
  N2: Part1.D5_PWM, L298N1.IN1
  N3: Part1.D6_PWM, L298N1.ENA
  N4: Part1.D7, Mod1.S
  5V: Part1.5V, Mod1.Vin
  N5: Part1.GND, Mod1.-

custom parts:
  L298N DC motor driver: 2x DC motor driver with 78M05 positive voltage regulator (7..35 V) L298N: max 46 V, 2 A Set 5 V Enable jumper to enable 5 V regultor (needed for the L298N) and +5 V output at screw terminal or supply external +5 V at screw terminal Set ENA and/or ENB to +5 V to enable motor permanently or supply ENA and/or ENB with PWM signal IN1 and IN2 set rotation directory for motor A (OUT1/OUT2) IN2 and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
  KY-022 Infrared Receiver Module: KY-022 IR receiver module, reacts to 38kHz infrared light.
  LM2596 step down module: LM2596 DC-DC step down power supply module 3 A.
